# Fritzing sketch top (saved by Fritzing 0.7.5b)
breadboards: 2

parts:
  Arduino1 = Arduino
  IC2 = IC, DIP package, 14 pins [chip_label="TCA 871" spacing=300mil]
  R1 = Resistor [tolerance=±5% resistance=220 package=THT]
  R2 = Resistor [tolerance=±5% resistance=220 package=THT]
  R3 = Resistor [tolerance=±5% resistance=220 package=THT]
  R4 = Resistor [tolerance=±5% resistance=220 package=THT]
  R5 = Resistor [tolerance=±5% resistance=220 package=THT]
  U1 = AD5206 Digital Potentiometer [maximum_resistance=10kΩ package="SO28 [SMD]"]
  R6 = Resistor [tolerance=±5% resistance=220 package=THT]
  R7 = Resistor [tolerance=±5% resistance=220 package=THT]
  R8 = Resistor [tolerance=±5% resistance=220 package=THT]
  R9 = Resistor [tolerance=±5% resistance=220 package=THT]
  R10 = Resistor [tolerance=±5% resistance=220 package=THT]
  R11 = Resistor [tolerance=±5% resistance=220 package=THT]
  R12 = Resistor [tolerance=±5% resistance=220 package=THT]
  R13 = Resistor [tolerance=±5% resistance=220 package=THT]
  R14 = Resistor [tolerance=±5% resistance=220 package=THT]
  R15 = Resistor [tolerance=±5% resistance=220 package=THT]
  IC4 = IC, DIP package, 14 pins [chip_label="TCA 871" spacing=300mil]
  IC3 = IC, DIP package, 14 pins [chip_label="TCA 871" spacing=300mil]
  J1 = female pin header, 11 pins [form="♀ (female)"]
  J2 = female pin header, 3 pins [form="♀ (female)"]
  J3 = female pin header, 6 pins [form="♀ (female)"]
  J4 = female pin header, 5 pins [form="♀ (female)"]

nets:
  GND: Arduino1.GND, IC2.pin3, IC2.pin7, IC2.pin10, IC2.pin13, U1.B6, U1.Gnd, U1.Vss, U1.B5, U1.B3, U1.B1, U1.B2, U1.B4, IC4.pin3, IC4.pin7, IC4.pin10, IC4.pin13, IC3.pin3, IC3.pin7, IC3.pin10, IC3.pin13, J4.pin4
  N1: Arduino1.D13, U1.CLK
  N2: Arduino1.D12, R9.Pin_0
  N3: Arduino1.D11, U1.SDI
  N4: Arduino1.D10, U1.CS
  N5: Arduino1.D9, R10.Pin_0
  N6: Arduino1.D8, R15.Pin_0
  N7: Arduino1.D7, R11.Pin_0
  N8: Arduino1.D6, R12.Pin_0
  N9: Arduino1.D5, R13.Pin_0
  N10: Arduino1.D4, R14.Pin_0
  N11: Arduino1.D3, R7.Pin_0
  N12: Arduino1.D2, R6.Pin_0
  3V3: Arduino1.3V3, U1.Vdd, J1.pin6
  N13: Arduino1.A0, R8.Pin_0
  N14: Arduino1.A1, R4.Pin_0
  N15: Arduino1.A2, R3.Pin_0
  N16: Arduino1.A3, R2.Pin_0
  N17: Arduino1.A4, R1.Pin_0
  N18: Arduino1.A5, R5.Pin_0
  N19: IC2.pin1, J2.pin2
  N20: IC2.pin2, R2.Pin_1
  N21: IC2.pin4, R1.Pin_1
  N22: IC2.pin5, J2.pin1
  N23: IC2.pin6, R5.Pin_1
  N24: IC2.pin8, J3.pin5
  N25: IC2.pin9, R6.Pin_1
  N26: IC2.pin11, J3.pin6
  N27: IC2.pin12, R7.Pin_1
  N28: IC2.pin14, J3.pin4
  N29: R3.Pin_1, IC4.pin9
  N30: R4.Pin_1, IC4.pin12
  N31: U1.A6, U1.A5, J1.pin5
  N32: U1.W6, J1.pin4
  N33: U1.W5, J4.pin1
  N34: U1.W3, J4.pin3
  N35: U1.A3, U1.A1, U1.A2, U1.A4, J1.pin2
  N36: U1.W1, J4.pin2
  N37: U1.W2, J1.pin1
  N38: U1.W4, J1.pin3
  N39: R8.Pin_1, IC3.pin6
  N40: R9.Pin_1, IC4.pin6
  N41: R10.Pin_1, IC4.pin4
  N42: R11.Pin_1, IC3.pin4
  N43: R12.Pin_1, IC3.pin2
  N44: R13.Pin_1, IC3.pin12
  N45: R14.Pin_1, IC3.pin9
  N46: R15.Pin_1, IC4.pin2
  N47: IC4.pin1, J3.pin1
  N48: IC4.pin5, J4.pin5
  N49: IC4.pin8, J1.pin7
  N50: IC4.pin11, J1.pin8
  N51: IC4.pin14, J1.pin9
  N52: IC3.pin1, J3.pin2
  N53: IC3.pin5, J1.pin10
  N54: IC3.pin8, J1.pin11
  N55: IC3.pin11, J2.pin3
  N56: IC3.pin14, J3.pin3
